# Fritzing sketch Schematic (saved by Fritzing 0.9.6b)
breadboards: 1

parts:
  J2 = COMPUTER-PERIPHERAL-POWER [package=computer-peripheral-power-ra]
  J4 = COMPUTER-PERIPHERAL-POWER [package=computer-peripheral-power-ra]  # not connected
  D6 = Schottky Diode [part_number=1N5817 package="300 mil [THT]"]
  D11 = Schottky Diode [part_number=1N5817 package="300 mil [THT]"]
  U2 = Molex Picoblade Series Header [part_number=0533980471 package=Picoblade-53398-0471]
  U4 = ESP32-38PinWide [part_number=ESP32-38PinWide]
  Grove1 = Grove OLED 128x96
  S1 = Pushbutton [package="[THT]"]
  S2 = Pushbutton [package="[THT]"]
  U5 = Molex Picoblade Series Header [part_number=0533980471 package=Picoblade-53398-0471]
  U6 = Molex Picoblade Series Header [part_number=0533980471 package=Picoblade-53398-0471]
  U7 = Molex Picoblade Series Header [part_number=0533980471 package=Picoblade-53398-0471]
  U8 = Molex Picoblade Series Header [part_number=0533980471 package=Picoblade-53398-0471]
  U9 = Molex Picoblade Series Header [part_number=0533980471 package=Picoblade-53398-0471]

nets:
  12V: J2.12V, U4.VIN
  N1: J2.GND, J2.NC
  N2: D6.cathode, U2.2, U5.2, U6.2
  N3: D6.anode, D11.anode
  N4: D11.cathode, U7.2, U8.2, U9.2
  N5: U2.1, U5.1, U6.1
  N6: U2.4, U4.GPIO33, U5.4, U6.4
  N7: U4.3.3, Grove1.VCC
  GND: U4.GND, Grove1.GND, S1.Pin_3, S1.Pin_4, S2.Pin_3, S2.Pin_4, U7.1, U8.1, U9.1
  N8: U4.GPIO18, S1.Pin_1
  N9: U4.GPIO19, S2.Pin_1
  N10: U4.GPIO21, Grove1.SDA
  N11: U4.GPIO22, Grove1.SCL
  N12: U7.4, U9.4

notes:
  PSU #1
  FanSplitter #1
  FanSplitter #2
  FanSplitter #3
  FanSplitter #4
  FanSplitter #5
  FanSplitter #6

custom parts:
  ESP32-38PinWide: Generic 38-Pin ESP32 with wide format (only access to one side of pins on a breadboard) based on Stephen Lilley's HiLetgo ESP-WROOM-32 ESP32 ESP-32S Development Board.
